# Fritzing sketch sketch (saved by Fritzing 0.9.1b)
breadboards: 1

parts:
  Power_12v = Power plug
  Fuse = Fuse with Handler [part_number=GMA500mA]
  L7805CV = Voltage Regulator - 5V [package="TO220 [THT]"]
  Raspberry_Pi = Raspberry Pi B+
  Capacitor = Electrolytic Capacitor [capacitance=220µF voltage=16V package="300 mil [THT, electrolytic]"]
  IRLZ34N = NPN-Transistor [package="TO92 [THT]"]
  Led_strip = LED - 5mm [color="White (4500K)" package="5 mm [THT]"]
  Led_ready = LED - 5mm [color="Red (633nm)" package="5 mm [THT]"]
  S1 = Pushbutton [package=THT]
  R1 = Resistor [tolerance=±5% resistance=200 package=THT]

nets:
  N1: Power_12v.VCC, Fuse.Connector2, Led_strip.anode
  GND: Power_12v.GND, L7805CV.GND, Raspberry_Pi.GND, Capacitor.-, IRLZ34N.C, S1.leg0, R1.Pin_1
  N2: Fuse.Connector1, L7805CV.input_voltage
  N3: L7805CV.output_voltage, Raspberry_Pi.5V, Capacitor.+
  N4: Raspberry_Pi.GPIO17, IRLZ34N.E
  N5: Raspberry_Pi.GPIO27, Led_ready.anode
  N6: Raspberry_Pi.GPIO22, S1.leg1
  N7: IRLZ34N.B, Led_strip.cathode
  N8: Led_ready.cathode, R1.Pin_0
